# Fritzing sketch Botao-1 (saved by Fritzing 0.9.1b)
breadboards: 1

parts:
  Part1 = Arduino Uno (Rev3)
  LED1 = LED - 5mm [color="Red (633nm)" package="5 mm [THT]"]
  R1 = Resistor [tolerance=±5% resistance=220 package=THT]
  S1 = Pushbutton [package="[THT]"]
  R2 = Resistor [tolerance=±5% resistance=220 package=THT]

nets:
  N1: Part1.D12/MISO, S1.Pin_1, S1.Pin_2, R2.Pin_0
  N2: Part1.D13/SCK, R1.Pin_0
  N3: Part1.GND, LED1.cathode, R2.Pin_1
  N4: Part1.5V, S1.Pin_3, S1.Pin_4
  N5: LED1.anode, R1.Pin_1

// code stored in the sketch: Botao-1.ino
int led=13;      // led no pino 13
int botao=12;  // botão no pino 12
int var=0;       // valor instantaneo enviado pelo botão
int var2=0;     // valor guardado
int estado=0;  // guarda o valor 0 ou 1 (HIGH ou LOW)
void setup()
{
  pinMode(led,OUTPUT);
  pinMode(botao,INPUT);
}
void loop()
{
  var=digitalRead(botao); // ler o valor enviado pelo botão: "HIGH" ou "LOW"
  if ((var == HIGH) && (var2 == LOW)) {
    estado = 1 - estado;
    delay(20); // de-bouncing
  }
  var2=var;
  if (estado == 1) {
    digitalWrite(led, HIGH); // liga o led
  } else {
    digitalWrite(led, LOW);  // desliga o led
  }
}
