# Fritzing sketch Botao-2 (saved by Fritzing 0.9.1b)
breadboards: 1

parts:
  LED1 = RGB LED (com. cathode, rgb) [package="5 mm [THT]"]
  R1 = Resistor [tolerance=±5% resistance=220 package=THT]
  R2 = Resistor [tolerance=±5% resistance=220 package=THT]
  R3 = Resistor [tolerance=±5% resistance=220 package=THT]
  S1 = Pushbutton [package="[THT]"]
  S2 = Pushbutton [package="[THT]"]
  S3 = Pushbutton [package="[THT]"]
  R5 = Resistor [tolerance=±5% resistance=220 package=THT]
  Part1 = Arduino Uno (Rev3)
  R6 = Resistor [tolerance=±5% resistance=220 package=THT]
  R7 = Resistor [tolerance=±5% resistance=220 package=THT]

nets:
  N1: LED1.red_anode, R1.Pin_1
  N2: LED1.green_anode, R2.Pin_1
  N3: LED1.blue_anode, R3.Pin_1
  N4: R1.Pin_0, Part1.D10_PWM/SS
  N5: R2.Pin_0, Part1.D9_PWM
  N6: R3.Pin_0, Part1.D8
  N7: S1.Pin_1, S1.Pin_2, Part1.D5_PWM
  N8: S1.Pin_3, S1.Pin_4, S2.Pin_3, S2.Pin_4, R5.Pin_0, Part1.5V, R6.Pin_0, R7.Pin_0
  N9: S2.Pin_1, S2.Pin_2, Part1.D4
  N10: S3.Pin_1, S3.Pin_2
  N11: S3.Pin_3, S3.Pin_4
