# Fritzing sketch Buzzer-1 (saved by Fritzing 0.9.1b)
breadboards: 1

parts:
  Part1 = Arduino Uno (Rev3)
  SG1 = Buzzer 12mm [package=buzzer-12mm-ns]
  R1 = Resistor [tolerance=±5% resistance=100 package=THT]

nets:
  N1: Part1.D10_PWM/SS, R1.Pin_0
  N2: Part1.GND, SG1.1
  N3: SG1.2, R1.Pin_1

// code stored in the sketch: Buzzer-1.ino

const int buzzer = 10;
 
void setup() 
{
  pinMode(buzzer,OUTPUT);
}
 
void loop() 
{  
  //Ligando o buzzer com uma frequencia de 1500 hz.
  tone(buzzer,1500);   
  delay(500);
   
  //Desligando o buzzer.
  noTone(buzzer);
  delay(500);  
}
