# Fritzing sketch Display-1 (saved by Fritzing 0.9.1b)
breadboards: 1

parts:
  Part1 = Arduino Uno (Rev3)
  R1 = Rotary Potentiometer (Small) [maximum_resistance=100kΩ package=THT]
  LCD1 = LCD screen

nets:
  N1: Part1.D11_PWM/MOSI, LCD1.E
  N2: Part1.D12/MISO, LCD1.RS
  GND: Part1.GND, LCD1.VSS, LCD1.LED-
  N3: Part1.D2, LCD1.DB7
  N4: Part1.D3_PWM, LCD1.DB6
  N5: Part1.D4, LCD1.DB5
  N6: Part1.D5_PWM, LCD1.DB4
  5V: Part1.5V, R1.leg2, LCD1.VDD, LCD1.R/W, LCD1.LED+
  N7: R1.wiper, LCD1.V0

// code stored in the sketch: Display-1.ino
#include <LiquidCrystal.h> //Inclui a biblioteca do LCD
 
LiquidCrystal lcd(12, 11, 5, 4, 3, 2); //Configura os pinos do Arduino para se comunicar com o LCD
 
int temp; //Inicia uma variável inteira(temp), para escrever no LCD a contagem do tempo
 
void setup()
{

lcd.begin(16, 2); //Inicia o LCD com dimensões 16x2(Colunas x Linhas)
lcd.setCursor(0, 0); //Posiciona o cursor na primeira coluna(0) e na primeira linha(0) do LCD
lcd.print("Ola Garagista!"); //Escreve no LCD "Olá Garagista!"
lcd.setCursor(0, 1); //Posiciona o cursor na primeira coluna(0) e na segunda linha(1) do LCD
lcd.print("LabdeGaragem"); //Escreve no LCD "LabdeGaragem"
 
}
 
void loop()
{

lcd.setCursor(13, 1); //Posiciona o cursor na décima quarta coluna(13) e na segunda linha(1) do LCD
lcd.print(temp); //Escreve o valor atual da variável de contagem no LCD
delay(1000); //Aguarda 1 segundo
temp++; //Incrementa variável de contagem
 
if(temp == 600) //Se a variável temp chegar em 600(10 Minutos),...
  {
  temp = 0; //...zera a variável de contagem
  }

}
