# Fritzing sketch Led-2 (saved by Fritzing 0.9.1b)
breadboards: 1

parts:
  Part1 = Arduino Uno (Rev3)
  R1 = Resistor [tolerance=±5% resistance=1k package=THT]
  LED1 = LED - 5mm [color="Red (633nm)" package="5 mm [THT]"]

nets:
  N1: Part1.D13/SCK, R1.Pin_1
  N2: Part1.GND, LED1.cathode
  N3: R1.Pin_0, LED1.anode

notes:
  Feito: 15.0.2015
  Revisado: 15.02.2015

// code stored in the sketch: Led-2.ino

int iVerde = 13;  
  
void setup ()  
{  
   pinMode ( iVerde, OUTPUT );   
}  

void loop () 
{ 
   digitalWrite ( iVerde, HIGH ); 
   delay ( 1000 ); 
   digitalWrite ( iVerde, LOW ); 
   delay ( 1000 ); 
}
