# Fritzing sketch Led-3 (saved by Fritzing 0.9.1b)
breadboards: 1

parts:
  Part1 = Arduino Uno (Rev3)
  R1 = Resistor [tolerance=±5% resistance=220 package=THT]
  LED1 = LED - 5mm [color="Red (633nm)" package="5 mm [THT]"]
  R2 = Resistor [tolerance=±5% resistance=220 package=THT]
  LED2 = LED - 5mm [color="Red (633nm)" package="5 mm [THT]"]
  R3 = Resistor [tolerance=±5% resistance=220 package=THT]
  LED3 = LED - 5mm [color="Red (633nm)" package="5 mm [THT]"]

nets:
  N1: Part1.D11_PWM/MOSI, R3.Pin_1
  N2: Part1.D12/MISO, R2.Pin_1
  N3: Part1.D13/SCK, R1.Pin_1
  N4: Part1.GND, LED1.cathode, LED2.cathode, LED3.cathode
  N5: R1.Pin_0, LED1.anode
  N6: R2.Pin_0, LED2.anode
  N7: R3.Pin_0, LED3.anode

// code stored in the sketch: Led-3.ino
/*
** Definindo os Pinos a serem usados
*/

int iVerde = 13;  
int iVermelho = 12;  
int iAzul = 11;  

/*
** Definindo a Direcao do Pino
*/
  
void setup ()  
{  
   pinMode ( iVerde, OUTPUT );  
   pinMode ( iVermelho, OUTPUT );  
   pinMode ( iAzul, OUTPUT );  
}  

/*
** Programa Exemplo de Controle dos Pinos
*/

void loop () 
{ 
   digitalWrite ( iVerde, HIGH ); 
   delay ( 1000 ); 
   digitalWrite ( iVerde, LOW ); 
   delay ( 1000 ); 
 
   digitalWrite ( iVermelho, HIGH ); 
   delay ( 2000 ); 
   digitalWrite ( iVermelho, LOW ); 
   delay ( 2000 ); 
 
   digitalWrite ( iAzul, HIGH ); 
   delay ( 3000 ); 
   digitalWrite ( iAzul, LOW ); 
   delay ( 3000 ); 
}
