# Fritzing sketch Led-4 (saved by Fritzing 0.9.1b)
breadboards: 1

parts:
  Part1 = Arduino Uno (Rev3)
  R1 = Resistor [tolerance=±5% resistance=220 package=THT]
  LED1 = LED - 5mm [color="Red (633nm)" package="5 mm [THT]"]
  S2 = Pushbutton [package=THT]

nets:
  N1: Part1.D13/SCK, S2.leg0
  N2: Part1.GND, LED1.cathode
  N3: R1.Pin_0, LED1.anode
  N4: R1.Pin_1, S2.leg1
