# Fritzing sketch Led-5 (saved by Fritzing 0.9.1b)
breadboards: 1

parts:
  Part1 = Arduino Uno (Rev3)
  R1 = Resistor [tolerance=±5% resistance=220 package=THT]
  R2 = Resistor [tolerance=±5% resistance=220 package=THT]
  R3 = Resistor [tolerance=±5% resistance=220 package=THT]
  LED1 = RGB LED (com. cathode, rgb) [package="5 mm [THT]"]

nets:
  N1: Part1.D9_PWM, R3.Pin_0
  N2: Part1.D10_PWM/SS, R2.Pin_0
  N3: Part1.D11_PWM/MOSI, R1.Pin_0
  N4: Part1.GND, LED1.common_cathode
  N5: R1.Pin_1, LED1.blue_anode
  N6: R2.Pin_1, LED1.green_anode
  N7: R3.Pin_1, LED1.red_anode

// code stored in the sketch: Led-5.ino
int redpin=9;      //Pin 9
int greenpin=10;   //Pin 10
int bluepin=11;    //Pin 11
int var=0;
int var1=0;


void setup()
{
}

void loop()
{
  for(var=250;var<255;var++)
  {
  analogWrite(redpin,var);  //RED
  analogWrite(greenpin,0);
  delay(500);
  analogWrite(redpin,0);    //GREEN
  analogWrite(greenpin,var);
  delay(500);
  analogWrite(greenpin,0);   //BLUE
  analogWrite(bluepin,var);
  delay(500);
  analogWrite(bluepin,0);
  delay(500);
  }
  
  for(var1=250;var1<255;var1++)
  {
  analogWrite(redpin,var1);   //YELLOW
  analogWrite(greenpin,var1);
  delay(500);
  analogWrite(redpin,0);
  delay(500);
  analogWrite(greenpin,var1);  //CYAN
  analogWrite(bluepin,var1);
  delay(500);
  analogWrite(greenpin,0);
  delay(500);
  analogWrite(bluepin,var1);    //MAGENTA
  analogWrite(redpin,var1);
  delay(500);
  analogWrite(bluepin,0);
  delay(500);
  analogWrite(bluepin,var1);
  analogWrite(redpin,var1);
  analogWrite(greenpin,var1);
  }
  
}
