# Fritzing sketch Led-6 (saved by Fritzing 0.9.1b)
circuit board: 8.46667cm x 5.64444cm
breadboards: 1

parts:
  Part1 = Arduino Uno (Rev3)
  LED1 = RGB LED (com. cathode, rgb) [package="5 mm [THT]"]
  R1 = Resistor [tolerance=±5% resistance=270 package=THT]
  R2 = Resistor [tolerance=±5% resistance=270 package=THT]
  R3 = Resistor [tolerance=±5% resistance=270 package=THT]

nets:
  N1: Part1.D11_PWM/MOSI, R2.Pin_0
  N2: Part1.D12/MISO, R3.Pin_0
  N3: Part1.D13/SCK, R1.Pin_0
  N4: Part1.GND, LED1.common_cathode
  N5: LED1.red_anode, R1.Pin_1
  N6: LED1.green_anode, R3.Pin_1
  N7: LED1.blue_anode, R2.Pin_1

notes:
  Feito = 15.02.2015
  Revisado = 15.02.2015

// code stored in the sketch: Led-5.ino
int redpin=9;      //Pin 9
int greenpin=10;   //Pin 10
int bluepin=11;    //Pin 11
int var=0;
int var1=0;


void setup()
{
}

void loop()
{
  for(var=250;var<255;var++)
  {
  analogWrite(redpin,var);  //RED
  analogWrite(greenpin,0);
  delay(500);
  analogWrite(redpin,0);    //GREEN
  analogWrite(greenpin,var);
  delay(500);
  analogWrite(greenpin,0);   //BLUE
  analogWrite(bluepin,var);
  delay(500);
  analogWrite(bluepin,0);
  delay(500);
  }
  
  for(var1=250;var1<255;var1++)
  {
  analogWrite(redpin,var1);   //YELLOW
  analogWrite(greenpin,var1);
  delay(500);
  analogWrite(redpin,0);
  delay(500);
  analogWrite(greenpin,var1);  //CYAN
  analogWrite(bluepin,var1);
  delay(500);
  analogWrite(greenpin,0);
  delay(500);
  analogWrite(bluepin,var1);    //MAGENTA
  analogWrite(redpin,var1);
  delay(500);
  analogWrite(bluepin,0);
  delay(500);
  analogWrite(bluepin,var1);
  analogWrite(redpin,var1);
  analogWrite(greenpin,var1);
  }
  
}

// code stored in the sketch: Led-6.ino
/*
https://learn.adafruit.com/adafruit-arduino-lesson-3-rgb-leds/arduino-sketch
*/
 
int redPin = 11;
int greenPin = 10;
int bluePin = 9;
 
//uncomment this line if using a Common Anode LED
//#define COMMON_ANODE
 
void setup()
{
  pinMode(redPin, OUTPUT);
  pinMode(greenPin, OUTPUT);
  pinMode(bluePin, OUTPUT);  
}
 
void loop()
{
  setColor(255, 0, 0);  // red
  delay(1000);
  setColor(0, 255, 0);  // green
  delay(1000);
  setColor(0, 0, 255);  // blue
  delay(1000);
  setColor(255, 255, 0);  // yellow
  delay(1000);
}
 
void setColor(int red, int green, int blue)
{

  analogWrite(redPin, red);
  analogWrite(greenPin, green);
  analogWrite(bluePin, blue);  
}
