# Fritzing sketch Led-7 (saved by Fritzing 0.9.1b)
breadboards: 1

parts:
  Part1 = Arduino Uno (Rev3)
  R1 = Resistor [tolerance=±5% resistance=1k package=THT]
  R2 = Resistor [tolerance=±5% resistance=1k package=THT]
  S1 = Pushbutton [package="[THT]"]
  LED1 = LED - 5mm [color="Green (560nm)" package="5 mm [THT]"]
  LED2 = LED - 5mm [color="Red (633nm)" package="5 mm [THT]"]

nets:
  N1: Part1.D9_PWM, R2.Pin_0
  N2: Part1.D10_PWM/SS, R1.Pin_0
  N3: Part1.D2, Part1.5V, S1.Pin_1, S1.Pin_2, S1.Pin_3, S1.Pin_4, LED1.anode, LED2.anode
  N4: R1.Pin_1, LED1.cathode
  N5: R2.Pin_1, LED2.cathode

notes:
  Feito: 15.02.2015
  Revisado: 15.02.2015

// code stored in the sketch: Led-7.ino
int buttonPin=2;                    
int greenLED=9;                    
int redLED=10;                         

void setup()
{
  pinMode(buttonPin, INPUT);           
  pinMode(greenLED, OUTPUT);        
  pinMode(redLED, OUTPUT);             
}

void loop()
{
  digitalWrite(greenLED, HIGH);      
  digitalWrite(redLED, HIGH);    
    
  if (digitalRead(buttonPin)==LOW)
  {     
    digitalWrite(greenLED, LOW);      
    digitalWrite(redLED, LOW);         
  } 
}
