# Fritzing sketch Led-9 (saved by Fritzing 0.9.1b)
breadboards: 1

parts:
  S1 = Pushbutton [package="[THT]"]
  LED1 = LED - 5mm [color="Red (633nm)" package="5 mm [THT]"]
  LED3 = LED - 5mm [color="Red (633nm)" package="5 mm [THT]"]
  LED4 = LED - 5mm [color="Red (633nm)" package="5 mm [THT]"]
  R3 = Resistor [tolerance=±5% resistance=220 package=THT]
  R4 = Resistor [tolerance=±5% resistance=220 package=THT]
  R5 = Resistor [tolerance=±5% resistance=220 package=THT]
  Componente1 = Arduino Uno (Rev3)

nets (from the schematic view):
  N1: S1.Pin_1, S1.Pin_2, R3.Pin_0, R4.Pin_0, R5.Pin_0, Componente1.D13/SCK
  N2: S1.Pin_3, S1.Pin_4, Componente1.D6_PWM
  N3: LED1.cathode, R3.Pin_1
  N4: LED1.anode, Componente1.D3_PWM
  N5: LED3.cathode, R4.Pin_1
  N6: LED3.anode, Componente1.D4
  N7: LED4.cathode, R5.Pin_1
  N8: LED4.anode, Componente1.D5_PWM
