# Fritzing sketch Luminosidade-1 (saved by Fritzing 0.9.1b)
breadboards: 1

parts:
  Part1 = Arduino Uno (Rev3)
  R1 = Photocell (LDR) [package=THT]
  R2 = Resistor [tolerance=±5% resistance=150 package=THT]
  R3 = Resistor [tolerance=±5% resistance=150 package=THT]
  LED1 = LED - 5mm [color="Red (633nm)" package="5 mm [THT]"]

nets:
  N1: Part1.A2, R1.pin_0, R2.Pin_1
  N2: Part1.D10_PWM/SS, R3.Pin_1
  N3: Part1.5V, R1.pin_1
  N4: Part1.GND, R2.Pin_0, LED1.cathode
  N5: R3.Pin_0, LED1.anode

// code stored in the sketch: Luminosidade-1.ino
int valor = 0;  //Variável que receberá o valor do LDR
int led_pin = 10; // Pino do LED
int analogin = A2; // Pino em será ligado o LDR 

void setup(){
  Serial.begin(9600); 
  pinMode(led_pin, OUTPUT); 
}

void loop()
{
  valor = analogRead(analogin); // A variável valor recebe o valor do LDR
  Serial.println("O valor Da LDR e igual a: ");
  Serial.println ( valor); // Valor será mostrado no Serial Monitor
  delay(250); // Faz uma pausa de 250 milissegundos
  
  if (valor < 30) // Se o valor for menor que 30
  { 
	digitalWrite(led_pin, HIGH); // acende o led da porta 10
  } 
  else
  {                       //Caso seja maior 
    digitalWrite(led_pin, LOW); //apaga o LED
  } 
}
