# Fritzing sketch Potenciometro-1 (saved by Fritzing 0.9.1b)
breadboards: 1

parts:
  Part1 = Arduino Uno (Rev3)
  R1 = Rotary Potentiometer (Small) [maximum_resistance=100kΩ package=THT]

nets:
  N1: Part1.A1, R1.wiper
  N2: Part1.5V, R1.leg1
  N3: Part1.GND, R1.leg2

// code stored in the sketch: Potenciometro-1.ino
int viPot;
int pinPot = A1;

void setup ()
{
	Serial.begin (9600);
}

void loop ()
{
	viPot = analogRead (pinPot);
	Serial.print ( "Potenciometro: ");
	Serial.println (viPot);
	delay (100);
}
