# Fritzing sketch Potenciometro-2 (saved by Fritzing 0.9.1b)
breadboards: 1

parts:
  Part1 = Arduino Uno (Rev3)
  R1 = Rotary Potentiometer (Small) [maximum_resistance=100kΩ package=THT]
  LED1 = LED - 5mm [color="Red (633nm)" package="5 mm [THT]"]
  R2 = Resistor [tolerance=±5% resistance=150 package=THT]

nets:
  N1: Part1.A0, R1.wiper
  N2: Part1.D6_PWM, LED1.anode
  N3: Part1.5V, R1.leg1
  N4: R1.leg2, R2.Pin_0
  N5: LED1.cathode, R2.Pin_1

// code stored in the sketch: Potenciometro-2.ino
//
// http://www.ajudino.com/2013/04/3-utilizando-potenciometro-no-arduino.html
//
int potenciometro = 0;	// Define o pino do Arduino que o potenciômetro está conectado
int valor = 0;   		//Variável que irá receber o valor do potenciômetro
int led = 6 ; 			// Define o pino do Arduino que o led está conectado

void setup() 
{
  Serial.begin(9600);
  pinMode(led, OUTPUT);	// Seta a porta do led como saída
}

void loop() 
{
  valor = analogRead(potenciometro);	//Recebe o valor do potenciômetro
  if(valor > 0)
  {
    analogWrite(led, (valor/4));		//Acende o led com intensidade proporcional ao valor obtido
    Serial.println(valor); 				//Mostra no Serial Monitor o valor obtido do potenciômetro
  }
}
