# Fritzing sketch Led-6 (saved by Fritzing 0.9.1b)
breadboards: 1

parts:
  Part1 = Arduino Uno (Rev3)
  LED1 = RGB LED (com. cathode, rgb) [package="5 mm [THT]"]
  R1 = Resistor [tolerance=±5% resistance=220 package=THT]
  R2 = Resistor [tolerance=±5% resistance=220 package=THT]
  R3 = Resistor [tolerance=±5% resistance=220 package=THT]
  R4 = Resistor [tolerance=±5% resistance=220 package=THT]

nets:
  N1: Part1.GND, R4.Pin_0
  N2: Part1.D3_PWM, R1.Pin_0
  N3: Part1.D5_PWM, R2.Pin_0
  N4: Part1.D6_PWM, R3.Pin_0
  N5: LED1.red_anode, R1.Pin_1
  N6: LED1.common_cathode, R4.Pin_1
  N7: LED1.green_anode, R3.Pin_1
  N8: LED1.blue_anode, R2.Pin_1

// code stored in the sketch: Led-5.ino
int redpin=9;      //Pin 9
int greenpin=10;   //Pin 10
int bluepin=11;    //Pin 11
int var=0;
int var1=0;


void setup()
{
}

void loop()
{
  for(var=250;var<255;var++)
  {
  analogWrite(redpin,var);  //RED
  analogWrite(greenpin,0);
  delay(500);
  analogWrite(redpin,0);    //GREEN
  analogWrite(greenpin,var);
  delay(500);
  analogWrite(greenpin,0);   //BLUE
  analogWrite(bluepin,var);
  delay(500);
  analogWrite(bluepin,0);
  delay(500);
  }
  
  for(var1=250;var1<255;var1++)
  {
  analogWrite(redpin,var1);   //YELLOW
  analogWrite(greenpin,var1);
  delay(500);
  analogWrite(redpin,0);
  delay(500);
  analogWrite(greenpin,var1);  //CYAN
  analogWrite(bluepin,var1);
  delay(500);
  analogWrite(greenpin,0);
  delay(500);
  analogWrite(bluepin,var1);    //MAGENTA
  analogWrite(redpin,var1);
  delay(500);
  analogWrite(bluepin,0);
  delay(500);
  analogWrite(bluepin,var1);
  analogWrite(redpin,var1);
  analogWrite(greenpin,var1);
  }
  
}

// code stored in the sketch: Led-6.ino
// Firmware para Controle de Cores do LED RGB
#define RED 3 // Define o pino 3 com PWM como RED
#define BLUE 5 // Define o pino 5 com PWM como BLUE
#define GREEN 6 // Define o pino 6 com PWM como GREEN

int red = 255, green = 255, blue = 255; // valores de 0 a 255 (vari?-los para obter cores diferentes).

void setup() 
{
pinMode (RED, OUTPUT); // Pino 3 declarado como sa?da
pinMode (BLUE, OUTPUT); // Pino 5 declarado como sa?da
pinMode (GREEN, OUTPUT); // Pino 6 declarado como sa?da
}

void loop() 
}  
digitalWrite (GREEN, green);
digitalWrite (BLUE, blue);
digitalWrite (RED, red); 
}
