# Fritzing sketch Led-7 (saved by Fritzing 0.9.1b)
breadboards: 1

parts:
  Part1 = Arduino Uno (Rev3)
  R1 = Resistor [tolerance=±5% resistance=220 package=THT]
  R2 = Resistor [tolerance=±5% resistance=220 package=THT]
  S1 = Pushbutton [package="[THT]"]
  LED1 = LED - 5mm [color="Red (633nm)" package="5 mm [THT]"]
  LED2 = LED - 5mm [color="Red (633nm)" package="5 mm [THT]"]

nets:
  N1: Part1.D9_PWM, R2.Pin_0
  N2: Part1.D10_PWM/SS, R1.Pin_0
  N3: Part1.GND, Part1.D2, S1.Pin_1, S1.Pin_2, S1.Pin_3, S1.Pin_4
  N4: Part1.5V, LED1.anode, LED2.anode
  N5: R1.Pin_1, LED1.cathode
  N6: R2.Pin_1, LED2.cathode

// code stored in the sketch: Led-7.ino
/*
  Flip Flop
  switching between two LEDs using a button
  
  This example is part of the Fritzing Creator Kit: www.fritzing.org/creator-kit.
*/

int buttonPin=2;                       // Pin where the button is attached
int greenLED=9;                        // Pin where the green LED is attached
int redLED=10;                         // Pin where the red LED is attached 

void setup(){
  pinMode(buttonPin, INPUT);           // button is initialised as INPUT 
  pinMode(greenLED, OUTPUT);           // green LED pin is initialised as OUTPUT 
  pinMode(redLED, OUTPUT);             // red LED pin is initialised as OUTPUT  
}

void loop(){
  if (digitalRead(buttonPin)==LOW){    // if the button is pressed (LOW) 
    digitalWrite(greenLED, HIGH);      // switch on green LED
    digitalWrite(redLED, LOW);         // switch off red LED
  } else {                             // else (if button is not pressed)
    digitalWrite(greenLED, LOW);       // switch off green LED
    digitalWrite(redLED, HIGH);        // switch on red LED
  }
}
